# Fritzing sketch station (saved by Fritzing 0.9.6b)
breadboards: 1

parts:
  WeMos_D1_Mini1 = WeMos D1 Mini
  C2 = Capacitor Polarized [package=panasonic_g]
  C3 = Capacitor [package=cap-pth-small2]
  U1 = Voltage Regulator [package=to-92]
  BAT1 = 18650 battery holder [package=battery-18650-kit]

nets:
  N1: WeMos_D1_Mini1.3V3, C2.+, C3.2, U1.OUT
  N2: WeMos_D1_Mini1.G, C2.-, C3.1, U1.GND, BAT1.+
  N3: U1.IN, BAT1.-

custom parts:
  18650 battery holder: 18650 Battery Holder identical to the dual battery version.
