# Fritzing sketch station (saved by Fritzing 0.9.6b)
breadboards: 1

parts:
  WeMos_D1_Mini1 = WeMos D1 Mini
  DS1 = DS18B20 1-Wire Temperature Sensor [part_number=DS18B20]
  R1 = Resistor [tolerance=±5% power=0.25 resistance=10k package=THT]
  C2 = Capacitor Polarized [package=panasonic_g]
  C3 = Capacitor [package=cap-pth-small2]
  U1 = Voltage Regulator [package=to-92]
  U2 = LIPO-2000mAh [package=lipo-2000]

nets:
  3V3: WeMos_D1_Mini1.3V3, DS1.VDD, R1.Pin_1, C2.+, C3.2, U1.OUT
  N1: WeMos_D1_Mini1.D6, DS1.DQ, R1.Pin_0
  GND: WeMos_D1_Mini1.G, DS1.GND, C2.-, C3.1, U1.GND, U2.-
  N2: U1.IN, U2.+
