# Fritzing sketch lol (saved by Fritzing 1.0.1rc)
breadboards: 1

parts:
  A1 = Esp32-c3 super mini
  S1 = 0.91 inch OLED I2C Display 128 x 32 Pixels
  VCC1 = Battery
  S2 = Momentary Switch [package=ksa_sealed_tac_switch]
  R1 = Resistor [tolerance=±5% power=0.25 resistance=10k package=THT]

nets:
  N1: A1.Pin_9, S1.SCL
  N2: A1.Pin_10, S1.SDA
  N3: A1.Pin_13, S2.4
  N4: A1.Pin_14, S1.VCC, VCC1.+, R1.Pin_1
  N5: A1.Pin_15, S1.GND, VCC1.-
  N6: S2.1, R1.Pin_0

custom parts:
  Esp32-c3 super mini: ESP32-C3 Development Board ESP32 SuperMini Development Board ESP32 Development Board WiFi Bluetooth.
