# Fritzing sketch weather (saved by Fritzing 0.9.6b)
breadboards: 2

parts:
  U1 = ESP8266 NodeMCU LoLin module
  Деталь2 = BME280

nets:
  N1: U1.D0, U1.RST
  N2: U1.D1, Деталь2.SCL
  N3: U1.D2, Деталь2.SDA
  3V3: U1.3V3, Деталь2.VIN
  GND: U1.GND, U1.D6, Деталь2.GND

custom parts:
  ESP8266 NodeMCU LoLin module: ESP8266 based NodeMCU
