# Fritzing sketch base (saved by Fritzing 0.9.6b)
breadboards: 1

parts:
  WeMos_D1_Mini1 = WeMos D1 Mini
  R1 = Resistor [tolerance=±5% power=0.25 resistance=10k package=THT]
  DS1 = DS18B20 1-Wire Temperature Sensor [part_number=DS18B20]

nets:
  3V3: WeMos_D1_Mini1.3V3, R1.Pin_1, DS1.VDD
  N1: WeMos_D1_Mini1.D0, WeMos_D1_Mini1.RST
  N2: WeMos_D1_Mini1.D6, R1.Pin_0, DS1.DQ
  N3: WeMos_D1_Mini1.G, DS1.GND
